# Fritzing sketch low-cost_diy_keyboard_20251205 (saved by Fritzing 1.0.1rc)
perfboards: 1

parts:
  パーツ1 = UIAPduino Pro Micro CH32V003
  R1 = Resistor [tolerance=±5% power=0.25 resistance=180k package=THT]
  R2 = Resistor [tolerance=±5% power=0.25 resistance=6.8k package=THT]
  R3 = Resistor [tolerance=±5% power=0.25 resistance=6.8k package=THT]
  R4 = Resistor [tolerance=±5% power=0.25 resistance=6.8k package=THT]
  S2 = Round Pushbutton
  S3 = Round Pushbutton
  S4 = Round Pushbutton

nets:
  N1: パーツ1.3, パーツ1.4, パーツ1.23, R1.Pin_1
  N2: パーツ1.8, R2.Pin_1
  N3: パーツ1.10, パーツ1.16, R3.Pin_1
  N4: パーツ1.11, パーツ1.14, R4.Pin_1
  N5: パーツ1.12, パーツ1.15, R1.Pin_0
  N6: R2.Pin_0, S2.leg1
  N7: R3.Pin_0, S3.leg1
  N8: R4.Pin_0, S4.leg1

custom parts:
  UIAPduino Pro Micro CH32V003: Design: Yuuki Umeta, CC BY-SA 4.0 https://creativecommons.org/licenses/by-sa/4.0/
